# Fritzing sketch DHT22_Wiring (saved by Fritzing 0.9.3b)
breadboards: 1

parts:
  Raspberry_Pi_3 = Raspberry Pi 3 [part_number=RPI-3-V1.2]
  RHT22 = Humidity and Temperature Sensor RHT03
  R1 = Resistor [tolerance=±5% resistance=5k package=THT]

nets:
  3V3: Raspberry_Pi_3.3v3, RHT22.Vcc, R1.Pin_0
  N1: Raspberry_Pi_3.GND, RHT22.GND_2
  N2: Raspberry_Pi_3.GPIO18, RHT22.Data-signal, R1.Pin_1
